// Logisim project S1-T4.circ as structural Verilog: 18 circuits, main circuit main
module main (
  input  [7:0] in_1,
  input  sign_A,
  input  [7:0] in_3,
  input  sign_B,
  input  [7:0] in_5,
  input  sign_C,
  output [3:0] out_7,
  output out_8,
  output [7:0] out_9,
  output out_10,
  output [7:0] out_11,
  output out_12
);

  wire clock_1_out, root_calculation_1_out_8, root_calculation_1_out_10;
  wire [3:0] base_calculator_1_out_4;
  wire [7:0] base_converter_1_out_3, base_converter_2_out_3, base_converter_3_out_3,
       root_calculation_1_out_9, root_calculation_1_out_11;

  Hex_Digit_Display hex_digit_display_1 (.value(in_1[7:4]));  // open: dp
  Hex_Digit_Display hex_digit_display_2 (.value(in_3[7:4]));  // open: dp
  Hex_Digit_Display hex_digit_display_3 (.value(in_5[7:4]));  // open: dp
  Hex_Digit_Display hex_digit_display_4 (.value(in_1[3:0]));  // open: dp
  Hex_Digit_Display hex_digit_display_5 (.value(in_3[3:0]));  // open: dp
  Hex_Digit_Display hex_digit_display_6 (.value(in_5[3:0]));  // open: dp
  Base_Calculator base_calculator_1 (.in_1(in_1), .in_2(in_3), .in_3(in_5), .out_4(base_calculator_1_out_4));
  Clock clock_1 (.out(clock_1_out));
  Synchronous_Up_Counter synchronous_up_counter_1 (.in_2(base_calculator_1_out_4), .Clk(clock_1_out), .out_3(out_7));
  Base_Converter base_converter_1 (.b(out_7), .Y(in_1), .out_3(base_converter_1_out_3));
  Base_Converter base_converter_2 (.b(out_7), .Y(in_3), .out_3(base_converter_2_out_3));
  Base_Converter base_converter_3 (.b(out_7), .Y(in_5), .out_3(base_converter_3_out_3));
  Root_Calculation root_calculation_1 (
    .sign_A(sign_A), .in_2(base_converter_1_out_3), .sign_B(sign_B), .in_4(base_converter_2_out_3),
    .sign_C(sign_C), .in_6(base_converter_3_out_3), .out_7(out_8), .out_8(root_calculation_1_out_8),
    .out_9(root_calculation_1_out_9), .out_10(root_calculation_1_out_10), .out_11(root_calculation_1_out_11));
  Decimal_to_base decimal_to_base_1 (
    .sign_Root_1(root_calculation_1_out_8), .in_2(root_calculation_1_out_9),
    .in_3(root_calculation_1_out_10), .in_4(root_calculation_1_out_11), .out_5(out_10), .out_6(out_9),
    .out_7(out_12), .out_8(out_11));
  Hex_Digit_Display hex_digit_display_7 (.value(out_7));  // open: dp
  Hex_Digit_Display hex_digit_display_8 (.value(out_9[3:0]));  // open: dp
  Hex_Digit_Display hex_digit_display_9 (.value(out_9[7:4]));  // open: dp
  Hex_Digit_Display hex_digit_display_10 (.value(out_11[3:0]));  // open: dp
  Hex_Digit_Display hex_digit_display_11 (.value(out_11[7:4]));  // open: dp

  // Notes on the sheet:
  //   A
  //   B
  //   C
  //   Base Calculator
  //   Clk
  //   UniQuad System
  //   Base to Decimal
  //   Root Calculator
  //   Decimal to Base
  //   Base
  //   real_Roots
  //   Root_1
  //   sign_Root_1
  //   Root_2
  //   sign_Root_2
endmodule

module _4_bit_Comparator (
  input  [3:0] A,
  input  [3:0] B,
  output A___B,
  output out_4,
  output A___B_2
);

  wire and_1_out, and_2_out, and_3_out, and_4_out, and_5_out, and_6_out, and_7_out, and_8_out, and_9_out,
       and_10_out, and_11_out, and_12_out, and_13_out, and_14_out, nor_1_out, nor_2_out, nor_3_out,
       nor_4_out, not_1_out, not_2_out, not_3_out, not_4_out, not_5_out, not_6_out, not_7_out, not_8_out;

  not not_1 (not_1_out, A[3]);
  not not_2 (not_2_out, B[3]);
  not not_3 (not_3_out, A[2]);
  not not_4 (not_4_out, B[2]);
  not not_5 (not_5_out, A[1]);
  not not_6 (not_6_out, B[1]);
  not not_7 (not_7_out, A[0]);
  not not_8 (not_8_out, B[0]);
  and and_1 (and_1_out, not_1_out, B[3]);
  and and_2 (and_2_out, A[3], not_2_out);
  and and_3 (and_3_out, not_3_out, B[2]);
  and and_4 (and_4_out, A[2], not_4_out);
  and and_5 (and_5_out, not_5_out, B[1]);
  and and_6 (and_6_out, A[1], not_6_out);
  and and_7 (and_7_out, not_7_out, B[0]);
  and and_8 (and_8_out, A[0], not_8_out);
  nor nor_1 (nor_1_out, and_1_out, and_2_out);
  nor nor_2 (nor_2_out, and_3_out, and_4_out);
  nor nor_3 (nor_3_out, and_5_out, and_6_out);
  nor nor_4 (nor_4_out, and_7_out, and_8_out);
  and and_9 (and_9_out, nor_1_out, and_3_out);
  and and_10 (and_10_out, nor_1_out, and_4_out);
  and and_11 (and_11_out, nor_1_out, nor_2_out, and_5_out);
  and and_12 (and_12_out, nor_1_out, nor_2_out, and_6_out);
  and and_13 (and_13_out, nor_1_out, nor_2_out, nor_3_out, and_7_out);
  and and_14 (and_14_out, nor_1_out, nor_2_out, nor_3_out, and_8_out);
  and and_15 (out_4, nor_1_out, nor_2_out, nor_3_out, nor_4_out);
  or or_1 (A___B, and_1_out, and_9_out, and_11_out, and_13_out);
  or or_2 (A___B_2, and_2_out, and_10_out, and_12_out, and_14_out);

  // Notes on the sheet:
  //   4-Bit Comparator
  //   A = B
endmodule

module Max_Digit (
  input  [7:0] in_1,
  input  [7:0] in_2,
  input  [7:0] in_3,
  output [3:0] out_4
);

  wire n4_bit_comparator_1_a___b, n4_bit_comparator_2_a___b, n4_bit_comparator_3_a___b,
       n4_bit_comparator_4_a___b, n4_bit_comparator_5_a___b, n4_bit_comparator_6_a___b;
  wire [3:0] multiplexer_1_out, multiplexer_2_out, multiplexer_3_out, multiplexer_4_out, multiplexer_5_out;

  _4_bit_Comparator u_4_bit_comparator_1 (
    .A(4'b0001), .B(in_1[3:0]), .A___B(n4_bit_comparator_1_a___b));  // open: out_4, A___B_2
  _4_bit_Comparator u_4_bit_comparator_2 (
    .A(multiplexer_1_out), .B(in_1[7:4]), .A___B(n4_bit_comparator_2_a___b));  // open: out_4, A___B_2
  _4_bit_Comparator u_4_bit_comparator_3 (
    .A(multiplexer_2_out), .B(in_2[3:0]), .A___B(n4_bit_comparator_3_a___b));  // open: out_4, A___B_2
  _4_bit_Comparator u_4_bit_comparator_4 (
    .A(multiplexer_3_out), .B(in_2[7:4]), .A___B(n4_bit_comparator_4_a___b));  // open: out_4, A___B_2
  _4_bit_Comparator u_4_bit_comparator_5 (
    .A(multiplexer_4_out), .B(in_3[3:0]), .A___B(n4_bit_comparator_5_a___b));  // open: out_4, A___B_2
  _4_bit_Comparator u_4_bit_comparator_6 (
    .A(multiplexer_5_out), .B(in_3[7:4]), .A___B(n4_bit_comparator_6_a___b));  // open: out_4, A___B_2
  Multiplexer #(.width(4)) multiplexer_1 (
    .in0(4'b0001), .in1(in_1[3:0]), .out(multiplexer_1_out), .sel(n4_bit_comparator_1_a___b), .en(1'b1));
  Multiplexer #(.width(4)) multiplexer_2 (
    .in0(multiplexer_1_out), .in1(in_1[7:4]), .out(multiplexer_2_out), .sel(n4_bit_comparator_2_a___b),
    .en(1'b1));
  Multiplexer #(.width(4)) multiplexer_3 (
    .in0(multiplexer_2_out), .in1(in_2[3:0]), .out(multiplexer_3_out), .sel(n4_bit_comparator_3_a___b),
    .en(1'b1));
  Multiplexer #(.width(4)) multiplexer_4 (
    .in0(multiplexer_3_out), .in1(in_2[7:4]), .out(multiplexer_4_out), .sel(n4_bit_comparator_4_a___b),
    .en(1'b1));
  Multiplexer #(.width(4)) multiplexer_5 (
    .in0(multiplexer_4_out), .in1(in_3[3:0]), .out(multiplexer_5_out), .sel(n4_bit_comparator_5_a___b),
    .en(1'b1));
  Multiplexer #(.width(4)) multiplexer_6 (
    .in0(multiplexer_5_out), .in1(in_3[7:4]), .out(out_4), .sel(n4_bit_comparator_6_a___b), .en(1'b1));

  // Notes on the sheet:
  //   A
  //   B
  //   C
  //   Maximum Digit Calculator
  //   Maximum Digit
endmodule

module Base_Calculator (
  input  [7:0] in_1,
  input  [7:0] in_2,
  input  [7:0] in_3,
  output [3:0] out_4
);

  wire [3:0] max_digit_1_out_4;

  Max_Digit max_digit_1 (.in_1(in_1), .in_2(in_2), .in_3(in_3), .out_4(max_digit_1_out_4));
  Adder #(.width(4)) adder_1 (.a(max_digit_1_out_4), .b(4'b0001), .out(out_4));  // open: cin, cout

  // Notes on the sheet:
  //   Base Calculator
  //   A
  //   B
  //   C
  //   Minimum Base
endmodule

module Base_Converter (
  input  [3:0] b,
  input  [7:0] Y,
  output [7:0] out_3
);

  wire n4_bit_adder_1_cout;
  wire [3:0] multiplier_1_out_3, multiplier_1_out_4;

  Multiplier multiplier_1 (.A(b), .B(Y[7:4]), .out_4(multiplier_1_out_4), .out_3(multiplier_1_out_3));
  _4_Bit_Adder u_4_bit_adder_1 (
    .Cin(1'b0), .A0(multiplier_1_out_3[0]), .A1(multiplier_1_out_3[1]), .A2(multiplier_1_out_3[2]),
    .A3(multiplier_1_out_3[3]), .B0(Y[0]), .B1(Y[1]), .B2(Y[2]), .B3(Y[3]), .S0(out_3[0]), .S1(out_3[1]),
    .S2(out_3[2]), .S3(out_3[3]), .Cout(n4_bit_adder_1_cout));
  _4_Bit_Adder u_4_bit_adder_2 (
    .Cin(n4_bit_adder_1_cout), .A0(1'b0), .A1(1'b0), .A2(1'b0), .A3(1'b0), .B0(multiplier_1_out_4[0]),
    .B1(multiplier_1_out_4[1]), .B2(multiplier_1_out_4[2]), .B3(multiplier_1_out_4[3]), .S0(out_3[4]),
    .S1(out_3[5]), .S2(out_3[6]), .S3(out_3[7]));  // open: Cout

  // Notes on the sheet:
  //   Base Converter
  //   X
  //   Converted Number
  //   ( Xb + Y )
endmodule

module Multiplier (
  input  [3:0] A,
  input  [3:0] B,
  output [3:0] out_3,
  output [3:0] out_4
);

  wire and_1_out, and_2_out, and_3_out, and_4_out, and_5_out, and_6_out, and_7_out, and_8_out, and_9_out,
       and_10_out, and_11_out, and_12_out, and_13_out, and_14_out, and_16_out, n4_bit_adder_2_cout,
       n4_bit_adder_2_s1, n4_bit_adder_2_s2, n4_bit_adder_2_s3, n4_bit_adder_3_cout, n4_bit_adder_3_s1,
       n4_bit_adder_3_s2, n4_bit_adder_3_s3;

  and and_1 (and_1_out, B[3], A[3]);
  and and_2 (and_2_out, B[3], A[2]);
  and and_3 (and_3_out, B[3], A[1]);
  and and_4 (and_4_out, B[2], A[3]);
  and and_5 (and_5_out, B[3], A[0]);
  and and_6 (and_6_out, B[2], A[2]);
  _4_Bit_Adder u_4_bit_adder_1 (
    .Cin(1'b0), .A0(n4_bit_adder_2_s1), .A1(n4_bit_adder_2_s2), .A2(n4_bit_adder_2_s3),
    .A3(n4_bit_adder_2_cout), .B0(and_5_out), .B1(and_3_out), .B2(and_2_out), .B3(and_1_out), .S0(out_3[3]),
    .S1(out_4[0]), .S2(out_4[1]), .S3(out_4[2]), .Cout(out_4[3]));
  and and_7 (and_7_out, B[2], A[0]);
  and and_8 (and_8_out, B[2], A[1]);
  and and_9 (and_9_out, B[1], A[3]);
  and and_10 (and_10_out, B[1], A[2]);
  _4_Bit_Adder u_4_bit_adder_2 (
    .Cin(1'b0), .A0(n4_bit_adder_3_s1), .A1(n4_bit_adder_3_s2), .A2(n4_bit_adder_3_s3),
    .A3(n4_bit_adder_3_cout), .B0(and_7_out), .B1(and_8_out), .B2(and_6_out), .B3(and_4_out), .S0(out_3[2]),
    .S1(n4_bit_adder_2_s1), .S2(n4_bit_adder_2_s2), .S3(n4_bit_adder_2_s3), .Cout(n4_bit_adder_2_cout));
  and and_11 (and_11_out, B[1], A[1]);
  and and_12 (and_12_out, B[1], A[0]);
  _4_Bit_Adder u_4_bit_adder_3 (
    .Cin(1'b0), .A0(and_16_out), .A1(and_14_out), .A2(and_13_out), .A3(1'b0), .B0(and_12_out),
    .B1(and_11_out), .B2(and_10_out), .B3(and_9_out), .S0(out_3[1]), .S1(n4_bit_adder_3_s1),
    .S2(n4_bit_adder_3_s2), .S3(n4_bit_adder_3_s3), .Cout(n4_bit_adder_3_cout));
  and and_13 (and_13_out, B[0], A[3]);
  and and_14 (and_14_out, B[0], A[2]);
  and and_15 (out_3[0], B[0], A[0]);
  and and_16 (and_16_out, B[0], A[1]);

  // Notes on the sheet:
  //   4x4 Multiplier
  //   Product [7:4]
  //   Product [3:0]
endmodule

module Full_Adder (
  input  Cin,
  input  A,
  input  B,
  output Sum,
  output Carry
);

  wire and_1_out, and_2_out, and_3_out, xor_1_out;

  and and_1 (and_1_out, Cin, A);
  and and_2 (and_2_out, A, B);
  and and_3 (and_3_out, Cin, B);
  xor xor_1 (xor_1_out, Cin, A);
  or or_1 (Carry, and_1_out, and_2_out, and_3_out);
  xor xor_2 (Sum, xor_1_out, B);

  // Notes on the sheet:
  //   Full Adder
endmodule

module _4_Bit_Adder (
  input  Cin,
  input  A0,
  input  A1,
  input  A2,
  input  A3,
  input  B0,
  input  B1,
  input  B2,
  input  B3,
  output S0,
  output S1,
  output S2,
  output S3,
  output Cout
);

  wire full_adder_1_carry, full_adder_2_carry, full_adder_3_carry;

  Full_Adder full_adder_1 (.Cin(Cin), .A(A0), .B(B0), .Sum(S0), .Carry(full_adder_1_carry));
  Full_Adder full_adder_2 (.Cin(full_adder_1_carry), .A(A1), .B(B1), .Sum(S1), .Carry(full_adder_2_carry));
  Full_Adder full_adder_3 (.Cin(full_adder_2_carry), .A(A2), .B(B2), .Sum(S2), .Carry(full_adder_3_carry));
  Full_Adder full_adder_4 (.Cin(full_adder_3_carry), .A(A3), .B(B3), .Sum(S3), .Carry(Cout));

  // Notes on the sheet:
  //   4-Bit Adder
endmodule

module BCD_Adder (
  input  [3:0] A,
  input  [3:0] B,
  output [3:0] S0,
  output [3:0] S1
);

  wire and_1_out, and_2_out, n4_bit_adder_1_cout, n4_bit_adder_1_s0, n4_bit_adder_1_s1, n4_bit_adder_1_s2,
       n4_bit_adder_1_s3;

  _4_Bit_Adder u_4_bit_adder_1 (
    .Cin(1'b0), .A0(A[0]), .A1(A[1]), .A2(A[2]), .A3(A[3]), .B0(B[0]), .B1(B[1]), .B2(B[2]), .B3(B[3]),
    .S0(n4_bit_adder_1_s0), .S1(n4_bit_adder_1_s1), .S2(n4_bit_adder_1_s2), .S3(n4_bit_adder_1_s3),
    .Cout(n4_bit_adder_1_cout));
  and and_1 (and_1_out, n4_bit_adder_1_s3, n4_bit_adder_1_s1);
  and and_2 (and_2_out, n4_bit_adder_1_s3, n4_bit_adder_1_s2);
  or or_1 (S1[0], and_1_out, and_2_out, n4_bit_adder_1_cout);
  _4_Bit_Adder u_4_bit_adder_2 (
    .Cin(1'b0), .A0(1'b0), .A1(S1[0]), .A2(S1[0]), .A3(1'b0), .B0(n4_bit_adder_1_s0), .B1(n4_bit_adder_1_s1),
    .B2(n4_bit_adder_1_s2), .B3(n4_bit_adder_1_s3), .S0(S0[0]), .S1(S0[1]), .S2(S0[2]), .S3(S0[3]));  // open: Cout

  assign S1[3:1] = 3'b000;

  // Notes on the sheet:
  //   BCD Adder
endmodule

module Synchronous_Up_Counter (
  input  Clk,
  input  [3:0] in_2,
  output [3:0] out_3
);

  wire and_1_out, and_2_out, and_3_out, and_4_out, and_5_out, and_6_out, and_7_out, and_8_out, and_9_out,
       and_10_out, n4_bit_comparator_1_a___b_2, not_1_out, not_2_out, not_3_out, not_4_out;

  _4_bit_Comparator u_4_bit_comparator_1 (
    .A(in_2), .B(out_3), .A___B_2(n4_bit_comparator_1_a___b_2));  // open: A___B, out_4
  J_K_Flip_Flop j_k_ff_1 (
    .J(1'b1), .clk(Clk), .K(1'b1), .Q(out_3[0]), .preset(and_2_out), .reset(and_1_out));  // open: Qn, en
  and and_1 (and_1_out, not_1_out, n4_bit_comparator_1_a___b_2);
  and and_2 (and_2_out, in_2[0], n4_bit_comparator_1_a___b_2);
  not not_1 (not_1_out, in_2[0]);
  J_K_Flip_Flop j_k_ff_2 (
    .J(out_3[0]), .clk(Clk), .K(out_3[0]), .Q(out_3[1]), .preset(and_3_out), .reset(and_4_out));  // open: Qn, en
  and and_3 (and_3_out, in_2[1], n4_bit_comparator_1_a___b_2);
  and and_4 (and_4_out, not_2_out, n4_bit_comparator_1_a___b_2);
  not not_2 (not_2_out, in_2[1]);
  and and_5 (and_5_out, out_3[0], out_3[1]);
  J_K_Flip_Flop j_k_ff_3 (
    .J(and_5_out), .clk(Clk), .K(and_5_out), .Q(out_3[2]), .preset(and_6_out), .reset(and_7_out));  // open: Qn, en
  and and_6 (and_6_out, in_2[2], n4_bit_comparator_1_a___b_2);
  and and_7 (and_7_out, not_3_out, n4_bit_comparator_1_a___b_2);
  not not_3 (not_3_out, in_2[2]);
  and and_8 (and_8_out, and_5_out, out_3[2]);
  J_K_Flip_Flop j_k_ff_4 (
    .J(and_8_out), .clk(Clk), .K(and_8_out), .Q(out_3[3]), .preset(and_10_out), .reset(and_9_out));  // open: Qn, en
  and and_9 (and_9_out, not_4_out, n4_bit_comparator_1_a___b_2);
  and and_10 (and_10_out, in_2[3], n4_bit_comparator_1_a___b_2);
  not not_4 (not_4_out, in_2[3]);

  // Notes on the sheet:
  //   Preset
  //   Synchronous Up Counter
  //   Output
endmodule

module _8_bit_Comparator (
  input  [7:0] in_1,
  input  [7:0] in_2,
  output A___B,
  output A___B_2,
  output A___B_3
);

  wire and_1_out, and_3_out, n4_bit_comparator_1_a___b, n4_bit_comparator_1_a___b_2,
       n4_bit_comparator_1_out_4, n4_bit_comparator_2_a___b, n4_bit_comparator_2_a___b_2,
       n4_bit_comparator_2_out_4;

  _4_bit_Comparator u_4_bit_comparator_1 (
    .A(in_1[7:4]), .B(in_2[7:4]), .A___B(n4_bit_comparator_1_a___b), .out_4(n4_bit_comparator_1_out_4),
    .A___B_2(n4_bit_comparator_1_a___b_2));
  _4_bit_Comparator u_4_bit_comparator_2 (
    .A(in_1[3:0]), .B(in_2[3:0]), .A___B(n4_bit_comparator_2_a___b), .out_4(n4_bit_comparator_2_out_4),
    .A___B_2(n4_bit_comparator_2_a___b_2));
  or or_1 (A___B, n4_bit_comparator_1_a___b, and_1_out);
  and and_1 (and_1_out, n4_bit_comparator_1_out_4, n4_bit_comparator_2_a___b);
  and and_2 (A___B_2, n4_bit_comparator_1_out_4, n4_bit_comparator_2_out_4);
  and and_3 (and_3_out, n4_bit_comparator_2_out_4, n4_bit_comparator_2_a___b_2);
  or or_2 (A___B_3, and_3_out, n4_bit_comparator_1_a___b_2);

  // Notes on the sheet:
  //   8-Bit Comparator
  //   A
  //   B
endmodule

module Square_root (
  input  [7:0] in_1,
  output [3:0] out_2
);

  wire n8_bit_comparator_1_a___b, n8_bit_comparator_2_a___b, n8_bit_comparator_3_a___b,
       n8_bit_comparator_4_a___b, n8_bit_comparator_5_a___b, n8_bit_comparator_6_a___b,
       n8_bit_comparator_7_a___b, n8_bit_comparator_8_a___b, n8_bit_comparator_9_a___b,
       n8_bit_comparator_10_a___b, n8_bit_comparator_11_a___b, n8_bit_comparator_12_a___b,
       n8_bit_comparator_13_a___b, n8_bit_comparator_14_a___b, n8_bit_comparator_15_a___b,
       n8_bit_comparator_16_a___b, not_1_out, not_2_out, not_3_out, not_4_out, not_5_out, not_6_out,
       not_7_out, not_8_out, not_9_out, not_10_out, not_11_out, not_12_out, not_13_out, not_14_out,
       not_15_out, not_16_out;

  _8_bit_Comparator u_8_bit_comparator_1 (
    .in_1(in_1), .in_2({8{1'b0}}), .A___B(n8_bit_comparator_1_a___b));  // open: A___B_2, A___B_3
  _8_bit_Comparator u_8_bit_comparator_2 (
    .in_1(in_1), .in_2(8'h1), .A___B(n8_bit_comparator_2_a___b));  // open: A___B_2, A___B_3
  _8_bit_Comparator u_8_bit_comparator_3 (
    .in_1(in_1), .in_2(8'h4), .A___B(n8_bit_comparator_3_a___b));  // open: A___B_2, A___B_3
  _8_bit_Comparator u_8_bit_comparator_4 (
    .in_1(in_1), .in_2(8'h9), .A___B(n8_bit_comparator_4_a___b));  // open: A___B_2, A___B_3
  _8_bit_Comparator u_8_bit_comparator_5 (
    .in_1(in_1), .in_2(8'h10), .A___B(n8_bit_comparator_5_a___b));  // open: A___B_2, A___B_3
  _8_bit_Comparator u_8_bit_comparator_6 (
    .in_1(in_1), .in_2(8'h19), .A___B(n8_bit_comparator_6_a___b));  // open: A___B_2, A___B_3
  _8_bit_Comparator u_8_bit_comparator_7 (
    .in_1(in_1), .in_2(8'h24), .A___B(n8_bit_comparator_7_a___b));  // open: A___B_2, A___B_3
  _8_bit_Comparator u_8_bit_comparator_8 (
    .in_1(in_1), .in_2(8'h31), .A___B(n8_bit_comparator_8_a___b));  // open: A___B_2, A___B_3
  _8_bit_Comparator u_8_bit_comparator_9 (
    .in_1(in_1), .in_2(8'h40), .A___B(n8_bit_comparator_9_a___b));  // open: A___B_2, A___B_3
  _8_bit_Comparator u_8_bit_comparator_10 (
    .in_1(in_1), .in_2(8'h51), .A___B(n8_bit_comparator_10_a___b));  // open: A___B_2, A___B_3
  _8_bit_Comparator u_8_bit_comparator_11 (
    .in_1(in_1), .in_2(8'h64), .A___B(n8_bit_comparator_11_a___b));  // open: A___B_2, A___B_3
  _8_bit_Comparator u_8_bit_comparator_12 (
    .in_1(in_1), .in_2(8'h81), .A___B(n8_bit_comparator_12_a___b));  // open: A___B_2, A___B_3
  _8_bit_Comparator u_8_bit_comparator_13 (
    .in_1(in_1), .in_2(8'h90), .A___B(n8_bit_comparator_13_a___b));  // open: A___B_2, A___B_3
  _8_bit_Comparator u_8_bit_comparator_14 (
    .in_1(in_1), .in_2(8'ha9), .A___B(n8_bit_comparator_14_a___b));  // open: A___B_2, A___B_3
  _8_bit_Comparator u_8_bit_comparator_15 (
    .in_1(in_1), .in_2(8'hc4), .A___B(n8_bit_comparator_15_a___b));  // open: A___B_2, A___B_3
  _8_bit_Comparator u_8_bit_comparator_16 (
    .in_1(in_1), .in_2(8'he1), .A___B(n8_bit_comparator_16_a___b));  // open: A___B_2, A___B_3
  not not_1 (not_1_out, n8_bit_comparator_1_a___b);
  not not_2 (not_2_out, n8_bit_comparator_2_a___b);
  not not_3 (not_3_out, n8_bit_comparator_3_a___b);
  not not_4 (not_4_out, n8_bit_comparator_4_a___b);
  not not_5 (not_5_out, n8_bit_comparator_5_a___b);
  not not_6 (not_6_out, n8_bit_comparator_6_a___b);
  not not_7 (not_7_out, n8_bit_comparator_7_a___b);
  not not_8 (not_8_out, n8_bit_comparator_8_a___b);
  not not_9 (not_9_out, n8_bit_comparator_9_a___b);
  not not_10 (not_10_out, n8_bit_comparator_10_a___b);
  not not_11 (not_11_out, n8_bit_comparator_11_a___b);
  not not_12 (not_12_out, n8_bit_comparator_12_a___b);
  not not_13 (not_13_out, n8_bit_comparator_13_a___b);
  not not_14 (not_14_out, n8_bit_comparator_14_a___b);
  not not_15 (not_15_out, n8_bit_comparator_15_a___b);
  not not_16 (not_16_out, n8_bit_comparator_16_a___b);
  Priority_Encoder #(.select(4)) priority_encoder_1 (
    .in0(not_1_out), .in1(not_2_out), .in2(not_3_out), .in3(not_4_out), .in4(not_5_out), .in5(not_6_out),
    .in6(not_7_out), .in7(not_8_out), .in8(not_9_out), .in9(not_10_out), .in10(not_11_out),
    .in11(not_12_out), .in12(not_13_out), .in13(not_14_out), .in14(not_15_out), .in15(not_16_out),
    .out(out_2), .en_in(1'b1));  // open: gs, en_out

  // Notes on the sheet:
  //   8-Bit Input
  //   Square Root Calculator
  //   4-Bit Output
  //   ( Square Root )
endmodule

module _8_Bit_Adder_Subtractor (
  input  in_1,
  input  [7:0] in_2,
  input  [7:0] in_3,
  output [7:0] out_4
);

  wire n4_bit_adder_1_cout, xor_1_out, xor_2_out, xor_3_out, xor_4_out, xor_5_out, xor_6_out, xor_7_out,
       xor_8_out;

  xor xor_1 (xor_1_out, in_3[0], in_1);
  xor xor_2 (xor_2_out, in_3[1], in_1);
  xor xor_3 (xor_3_out, in_3[2], in_1);
  xor xor_4 (xor_4_out, in_3[3], in_1);
  xor xor_5 (xor_5_out, in_3[4], in_1);
  xor xor_6 (xor_6_out, in_3[5], in_1);
  xor xor_7 (xor_7_out, in_3[6], in_1);
  xor xor_8 (xor_8_out, in_3[7], in_1);
  _4_Bit_Adder u_4_bit_adder_1 (
    .Cin(in_1), .A0(in_2[0]), .A1(in_2[1]), .A2(in_2[2]), .A3(in_2[3]), .B0(xor_1_out), .B1(xor_2_out),
    .B2(xor_3_out), .B3(xor_4_out), .S0(out_4[0]), .S1(out_4[1]), .S2(out_4[2]), .S3(out_4[3]),
    .Cout(n4_bit_adder_1_cout));
  _4_Bit_Adder u_4_bit_adder_2 (
    .Cin(n4_bit_adder_1_cout), .A0(in_2[4]), .A1(in_2[5]), .A2(in_2[6]), .A3(in_2[7]), .B0(xor_5_out),
    .B1(xor_6_out), .B2(xor_7_out), .B3(xor_8_out), .S0(out_4[4]), .S1(out_4[5]), .S2(out_4[6]), .S3(out_4[7]));  // open: Cout

  // Notes on the sheet:
  //   A
  //   B
  //   8-Bit Adder cum Subtractor
  //   (Add)' / Subtract
  //   Output
endmodule

module Discriminant (
  input  sign_A,
  input  [7:0] in_2,
  input  sign_B,
  input  [7:0] in_4,
  input  sign_C,
  input  [7:0] in_6,
  output out_7,
  output [7:0] out_8
);

  wire n8_bit_comparator_1_a___b, n8_bit_comparator_1_a___b_2, or_1_out, xor_1_out, xor_2_out;
  wire [7:0] multiplexer_1_out, multiplexer_2_out, n8x8_multiplier_1_out_3, n8x8_multiplier_2_out_3,
       n8x8_multiplier_3_out_3;

  _8x8_Multiplier u_8x8_multiplier_1 (.in_1(in_2), .in_2(8'h4), .out_3(n8x8_multiplier_1_out_3));
  _8x8_Multiplier u_8x8_multiplier_2 (.in_1(in_4), .in_2(in_4), .out_3(n8x8_multiplier_2_out_3));
  xor xor_1 (xor_1_out, sign_A, sign_C);
  xor xor_2 (xor_2_out, 1'b1, xor_1_out);
  _8x8_Multiplier u_8x8_multiplier_3 (.in_1(n8x8_multiplier_1_out_3), .in_2(in_6), .out_3(n8x8_multiplier_3_out_3));
  _8_bit_Comparator u_8_bit_comparator_1 (
    .in_1(n8x8_multiplier_3_out_3), .in_2(n8x8_multiplier_2_out_3), .A___B(n8_bit_comparator_1_a___b),
    .A___B_2(n8_bit_comparator_1_a___b_2));  // open: A___B_3
  or or_1 (or_1_out, n8_bit_comparator_1_a___b, n8_bit_comparator_1_a___b_2);
  Multiplexer #(.width(8)) multiplexer_1 (
    .in0(n8x8_multiplier_3_out_3), .in1(n8x8_multiplier_2_out_3), .out(multiplexer_1_out), .sel(or_1_out),
    .en(1'b1));
  Multiplexer #(.width(8)) multiplexer_2 (
    .in0(n8x8_multiplier_2_out_3), .in1(n8x8_multiplier_3_out_3), .out(multiplexer_2_out), .sel(or_1_out),
    .en(1'b1));
  _8_Bit_Adder_Subtractor u_8_bit_adder_subtractor_1 (
    .in_2(multiplexer_1_out), .in_3(multiplexer_2_out), .in_1(xor_2_out), .out_4(out_8));
  Multiplexer multiplexer_3 (.in0(xor_2_out), .in1(1'b0), .out(out_7), .sel(or_1_out), .en(1'b1));

  // Notes on the sheet:
  //   A
  //   B
  //   C
  //   Discriminant Calculator
  //   sign_D
  //   D
endmodule

module _8x8_Multiplier (
  input  [7:0] in_1,
  input  [7:0] in_2,
  output [7:0] out_3
);

  wire [3:0] multiplier_1_out_3, multiplier_2_out_3, multiplier_2_out_4, multiplier_3_out_3,
       multiplier_3_out_4, multiplier_4_out_4;
  wire [7:0] n8_bit_adder_subtractor_1_out_4;
  wire [7:4] n8_bit_adder_subtractor_2_out_4;

  Multiplier multiplier_1 (.A(in_1[7:4]), .B(in_2[7:4]), .out_3(multiplier_1_out_3));  // open: out_4
  Multiplier multiplier_2 (.A(in_1[7:4]), .B(in_2[3:0]), .out_4(multiplier_2_out_4), .out_3(multiplier_2_out_3));
  Multiplier multiplier_3 (.A(in_1[3:0]), .B(in_2[7:4]), .out_4(multiplier_3_out_4), .out_3(multiplier_3_out_3));
  Multiplier multiplier_4 (.A(in_1[3:0]), .B(in_2[3:0]), .out_4(multiplier_4_out_4), .out_3(out_3[3:0]));
  _8_Bit_Adder_Subtractor u_8_bit_adder_subtractor_1 (
    .in_2({multiplier_2_out_4, multiplier_2_out_3}), .in_3({multiplier_3_out_4, multiplier_3_out_3}),
    .in_1(1'b0), .out_4(n8_bit_adder_subtractor_1_out_4));
  _8_Bit_Adder_Subtractor u_8_bit_adder_subtractor_2 (
    .in_2(n8_bit_adder_subtractor_1_out_4), .in_3({multiplier_1_out_3, multiplier_4_out_4}), .in_1(1'b0),
    .out_4({n8_bit_adder_subtractor_2_out_4, out_3[7:4]}));

  // Notes on the sheet:
  //   8x8 Multiplier
  //   A
  //   B
  //   Product
endmodule

module Root_Calculation (
  input  sign_A,
  input  [7:0] in_2,
  input  sign_B,
  input  [7:0] in_4,
  input  sign_C,
  input  [7:0] in_6,
  output out_7,
  output out_8,
  output [7:0] out_9,
  output out_10,
  output [7:0] out_11
);

  wire discriminant_1_out_7, multiplexer_3_out, multiplexer_6_out, n8_bit_comparator_1_a___b, not_1_out;
  wire [3:0] square_root_1_out_2;
  wire [7:0] discriminant_1_out_8, division_1_out_2, division_2_out_2, multiplexer_1_out, multiplexer_2_out,
       n8_bit_adder_subtractor_1_out_4, n8_bit_adder_subtractor_2_out_4;

  Discriminant discriminant_1 (
    .sign_A(sign_A), .in_2(in_2), .sign_B(sign_B), .in_4(in_4), .sign_C(sign_C), .in_6(in_6),
    .out_7(discriminant_1_out_7), .out_8(discriminant_1_out_8));
  _8_bit_Comparator u_8_bit_comparator_1 (
    .in_1({4'b0000, square_root_1_out_2}), .in_2(in_4), .A___B(n8_bit_comparator_1_a___b));  // open: A___B_2, A___B_3
  Square_root square_root_1 (.in_1(discriminant_1_out_8), .out_2(square_root_1_out_2));
  Multiplexer #(.width(8)) multiplexer_1 (
    .in0({4'b0000, square_root_1_out_2}), .in1(in_4), .out(multiplexer_1_out),
    .sel(n8_bit_comparator_1_a___b), .en(1'b1));
  Multiplexer #(.width(8)) multiplexer_2 (
    .in0(in_4), .in1({4'b0000, square_root_1_out_2}), .out(multiplexer_2_out),
    .sel(n8_bit_comparator_1_a___b), .en(1'b1));
  Multiplexer multiplexer_3 (
    .in0(1'b0), .in1(1'b1), .out(multiplexer_3_out), .sel(n8_bit_comparator_1_a___b), .en(1'b1));
  not not_1 (not_1_out, sign_B);
  _8_Bit_Adder_Subtractor u_8_bit_adder_subtractor_1 (
    .in_2(multiplexer_1_out), .in_3(multiplexer_2_out), .in_1(not_1_out),
    .out_4(n8_bit_adder_subtractor_1_out_4));
  Multiplexer multiplexer_4 (.in0(multiplexer_3_out), .in1(1'b0), .out(out_8), .sel(sign_B), .en(1'b1));
  Division division_1 (.in_1(n8_bit_adder_subtractor_1_out_4), .out_2(division_1_out_2));
  Multiplexer #(.width(8)) multiplexer_5 (
    .in0(division_1_out_2), .in1({8{1'b0}}), .out(out_9), .sel(discriminant_1_out_7), .en(1'b1));
  _8_Bit_Adder_Subtractor u_8_bit_adder_subtractor_2 (
    .in_2(multiplexer_1_out), .in_3(multiplexer_2_out), .in_1(sign_B), .out_4(n8_bit_adder_subtractor_2_out_4));
  Multiplexer multiplexer_6 (
    .in0(1'b1), .in1(1'b0), .out(multiplexer_6_out), .sel(n8_bit_comparator_1_a___b), .en(1'b1));
  Multiplexer multiplexer_7 (.in0(1'b1), .in1(multiplexer_6_out), .out(out_10), .sel(sign_B), .en(1'b1));
  Division division_2 (.in_1(n8_bit_adder_subtractor_2_out_4), .out_2(division_2_out_2));
  not not_2 (out_7, discriminant_1_out_7);
  Multiplexer #(.width(8)) multiplexer_8 (
    .in0(division_2_out_2), .in1({8{1'b0}}), .out(out_11), .sel(discriminant_1_out_7), .en(1'b1));

  // Notes on the sheet:
  //   Root Calculator
  //   A
  //   B
  //   C
  //   real_Roots
  //   sign_Root_1
  //   sign_Root_2
  //   Root_2
  //   Root_1
endmodule

module Division (
  input  [7:0] in_1,
  output [7:0] out_2
);


  assign out_2 = {1'b0, in_1[7:1]};

  // Notes on the sheet:
  //   Division by 2
  //   A
  //   Quotient
endmodule

module Decimal_to_base (
  input  sign_Root_1,
  input  [7:0] in_2,
  input  in_3,
  input  [7:0] in_4,
  output out_5,
  output [7:0] out_6,
  output out_7,
  output [7:0] out_8
);

  wire n8_bit_comparator_1_a___b, n8_bit_comparator_2_a___b;
  wire [7:0] multiplexer_1_out, multiplexer_2_out;
  wire [7:4] n8_bit_adder_subtractor_1_out_4, n8_bit_adder_subtractor_2_out_4;

  _8_bit_Comparator u_8_bit_comparator_1 (
    .in_1(in_2), .in_2(8'ha), .A___B(n8_bit_comparator_1_a___b));  // open: A___B_2, A___B_3
  _8_bit_Comparator u_8_bit_comparator_2 (
    .in_1(in_4), .in_2(8'ha), .A___B(n8_bit_comparator_2_a___b));  // open: A___B_2, A___B_3
  Multiplexer #(.width(8)) multiplexer_1 (
    .in0(8'ha), .in1({8{1'b0}}), .out(multiplexer_1_out), .sel(n8_bit_comparator_1_a___b), .en(1'b1));
  Multiplexer #(.width(8)) multiplexer_2 (
    .in0(8'ha), .in1({8{1'b0}}), .out(multiplexer_2_out), .sel(n8_bit_comparator_2_a___b), .en(1'b1));
  _8_Bit_Adder_Subtractor u_8_bit_adder_subtractor_1 (
    .in_2(in_2), .in_3(multiplexer_1_out), .in_1(1'b1), .out_4({n8_bit_adder_subtractor_1_out_4, out_6[3:0]}));
  _8_Bit_Adder_Subtractor u_8_bit_adder_subtractor_2 (
    .in_2(in_4), .in_3(multiplexer_2_out), .in_1(1'b1), .out_4({n8_bit_adder_subtractor_2_out_4, out_8[3:0]}));
  Multiplexer #(.width(4)) multiplexer_3 (
    .in0(4'b0001), .in1(4'b0000), .out(out_6[7:4]), .sel(n8_bit_comparator_1_a___b), .en(1'b1));
  Multiplexer #(.width(4)) multiplexer_4 (
    .in0(4'b0001), .in1(4'b0000), .out(out_8[7:4]), .sel(n8_bit_comparator_2_a___b), .en(1'b1));

  assign out_5 = sign_Root_1;
  assign out_7 = in_3;

  // Notes on the sheet:
  //   Root_1
  //   sign_Root_2
  //   Root_2
  //   Decimal to Base Convertor
  //   sign_Out_Root_1
  //   Out_Root_1
  //   sign_Out_Root_2
  //   Out_Root_2
endmodule
